# Fritzing sketch SonarScope (saved by Fritzing 0.9.2b)
breadboards: 1

parts:
  Part2 = HC-SR04 Ultrasonic Rangemeter
  J2 = Basic Servo
  JACK1 = 2.1mm Barrel Jack with Terminal Block
  Raspberry_Pi2 = Raspberry Pi 2
  TRINKET3 = Trinket 3V
  U3 = DIODE-ZENER [package=diode-zener]
  R3 = Resistor [tolerance=±5% resistance=1k package="0603 [SMD]"]

nets:
  VCC: Part2.VCC, Raspberry_Pi2.5V, TRINKET3.no_name_yet#1
  N1: Part2.Trig, TRINKET3.no_name_yet#4, U3.C, R3.Pin_0
  N2: Part2.Echo, R3.Pin_1
  GND: Part2.GND, J2.gnd, JACK1.NEG, Raspberry_Pi2.GND, TRINKET3.no_name_yet#2
  N3: J2.vcc, JACK1.POS
  N4: J2.pulse, TRINKET3.no_name_yet#3
  N5: Raspberry_Pi2.GPIO2, TRINKET3.no_name_yet#9
  N6: Raspberry_Pi2.GPIO3, TRINKET3.no_name_yet#7

custom parts:
  Trinket 3V: Adafruit Trinket 3V
  DIODE-ZENER: Zener Diode 3.3V Zener Voltage
